// Logisim project 1908034_Sabrina Sultana_control_sequencer.circ as structural Verilog: 11 circuits, main circuit main
module main (
  input  in_1,
  input  in_2,
  input  in_3,
  input  in_4,
  input  in_5,
  input  in_6,
  input  in_7,
  input  in_8,
  input  in_9,
  input  in_10,
  input  [7:0] in_11,
  input  in_12,
  output [7:0] out_13,
  output [7:0] out_14,
  output [7:0] out_15,
  output [7:0] out_16,
  output [7:0] out_17,
  output [7:0] out_18,
  output [7:0] out_19,
  output [7:0] out_20,
  output [7:0] out_21,
  output [7:0] out_22,
  output [7:0] out_23,
  output [7:0] out_24,
  output [7:0] out_25,
  output [7:0] out_26,
  output [7:0] out_27,
  output [7:0] out_28,
  output [7:0] out_29,
  output [7:0] out_30,
  output [7:0] out_31,
  output [7:0] out_32,
  output [3:0] out_33,
  output out_34,
  output out_35,
  output out_36,
  output out_37,
  output out_38,
  output [3:0] out_39,
  output out_40,
  output HLT,
  output [7:0] out_42
);

  wire AI, AO, BI, CE, CO, EO, II, IO, MI, not_1_out, OI, OO, RI, RO, SU;

  progcocus_1908034 progcocus_1908034_1 (
    .pc_en(CE), .pc_clk(in_9), .pc_reset(in_8), .pc_out_en(CO), .pc_out(out_15[3:0]));
  assign out_15 = in_10 ? in_11 : 8'bz;  // Controlled_Buffer controlled_buffer_1
  sram_1908034 sram_1908034_1 (
    .sram_wr(RI), .sram_rd(RO), .mar_d_in(out_15), .sram_d_in(out_15), .mar_in_en(MI), .sram_clk(in_9),
    .sram_d_out(out_15), .out_8(out_16), .out_9(out_17), .out_10(out_18), .out_11(out_19), .out_12(out_20),
    .out_13(out_21), .out_14(out_22), .out_15(out_23), .out_16(out_24), .out_17(out_26), .out_18(out_27),
    .out_19(out_28), .out_20(out_29), .out_21(out_30), .out_22(out_31), .out_23(out_32));
  not not_1 (not_1_out, in_10);
  regcus_1908034 regcus_1908034_1 (
    .reg_in(out_15), .reg_in_en(AI), .reg_clk(in_9), .reg_out_en(AO), .reg_int_out(out_13), .reg_out(out_15));
  ins_reg_1908034 ins_reg_1908034_1 (
    .ins_reg_in(out_15), .ins_reg_in_en(II), .clk(in_9), .ins_reg_out_en(IO), .add_outs(out_15[3:0]),
    .ins_out(out_39));
  regcus_1908034 regcus_1908034_2 (
    .reg_in(out_15), .reg_in_en(BI), .reg_clk(in_9), .reg_out_en(in_1), .reg_int_out(out_25), .reg_out(out_15));
  alucus_1908034 alucus_1908034_1 (
    .alu_in_1(out_13), .alu_out_en(EO), .alu_in_2(out_25), .alu_sub(SU), .alu_out(out_15));  // open: alu_cout
  controlsequencer_1908034 controlsequencer_1908034_1 (
    .clk(in_9), .clr(in_12), .in_3(out_39), .BI_en(not_1_out), .AI_en(not_1_out), .SU_en(not_1_out),
    .EO_en(not_1_out), .RI_en(not_1_out), .CO_en(not_1_out), .CE_en(not_1_out), .RO_en(not_1_out),
    .MI_en(not_1_out), .IO_en(not_1_out), .II_en(not_1_out), .OO_en(not_1_out), .OI_en(not_1_out),
    .AO_en(not_1_out), .t1(out_34), .t2(out_35), .t3(out_36), .t4(out_37), .t5(out_38), .t6(out_40),
    .out_24(HLT), .SU(SU), .CO(CO), .MI(MI), .AI(AI), .BI(BI), .EO(EO), .CE(CE), .II(II), .RO(RO), .OI(OI),
    .RI(RI), .OO(OO), .I0(IO), .AO(AO));
  assign RI = in_6 ? in_7 : 1'bz;  // Controlled_Buffer controlled_buffer_2
  assign OO = in_3 ? in_2 : 1'bz;  // Controlled_Buffer controlled_buffer_3
  assign MI = in_5 ? in_4 : 1'bz;  // Controlled_Buffer controlled_buffer_4
  regcus_1908034 regcus_1908034_3 (
    .reg_in(out_15), .reg_in_en(OI), .reg_clk(in_9), .reg_out_en(OO), .reg_int_out(out_14), .reg_out(out_15));

  assign out_33 = out_15[3:0];
  assign out_42 = out_15;

  // Other names for the same wires on the sheet: b_out = in_1; clk = in_9; clr = in_12; debug = in_10;
  //   debug_data[7:0] = in_11; pc_reset = in_8
endmodule

module regcus_1908034 (
  input  [7:0] reg_in,
  input  reg_in_en,
  input  reg_clk,
  input  reg_out_en,
  output [7:0] reg_int_out,
  output [7:0] reg_out
);

  wire multiplexer_1_out, multiplexer_2_out, multiplexer_3_out, multiplexer_4_out, multiplexer_5_out,
       multiplexer_6_out, multiplexer_7_out, multiplexer_8_out;

  Multiplexer multiplexer_1 (.in0(reg_int_out[7]), .in1(reg_in[7]), .out(multiplexer_1_out), .sel(reg_in_en));
  Multiplexer multiplexer_2 (.in0(reg_int_out[6]), .in1(reg_in[6]), .out(multiplexer_2_out), .sel(reg_in_en));
  D_Flip_Flop d_ff_1 (.D(multiplexer_1_out), .clk(reg_clk), .Q(reg_int_out[7]));  // open: Qn, preset, reset
  assign reg_out[7] = reg_out_en ? reg_int_out[7] : 1'bz;  // Controlled_Buffer controlled_buffer_1
  D_Flip_Flop d_ff_2 (.D(multiplexer_2_out), .clk(reg_clk), .Q(reg_int_out[6]));  // open: Qn, preset, reset
  Multiplexer multiplexer_3 (.in0(reg_int_out[5]), .in1(reg_in[5]), .out(multiplexer_3_out), .sel(reg_in_en));
  D_Flip_Flop d_ff_3 (.D(multiplexer_3_out), .clk(reg_clk), .Q(reg_int_out[5]));  // open: Qn, preset, reset
  assign reg_out[6] = reg_out_en ? reg_int_out[6] : 1'bz;  // Controlled_Buffer controlled_buffer_2
  Multiplexer multiplexer_4 (.in0(reg_int_out[4]), .in1(reg_in[4]), .out(multiplexer_4_out), .sel(reg_in_en));
  D_Flip_Flop d_ff_4 (.D(multiplexer_4_out), .clk(reg_clk), .Q(reg_int_out[4]));  // open: Qn, preset, reset
  assign reg_out[5] = reg_out_en ? reg_int_out[5] : 1'bz;  // Controlled_Buffer controlled_buffer_3
  Multiplexer multiplexer_5 (.in0(reg_int_out[3]), .in1(reg_in[3]), .out(multiplexer_5_out), .sel(reg_in_en));
  assign reg_out[4] = reg_out_en ? reg_int_out[4] : 1'bz;  // Controlled_Buffer controlled_buffer_4
  Multiplexer multiplexer_6 (.in0(reg_int_out[2]), .in1(reg_in[2]), .out(multiplexer_6_out), .sel(reg_in_en));
  D_Flip_Flop d_ff_5 (.D(multiplexer_5_out), .clk(reg_clk), .Q(reg_int_out[3]));  // open: Qn, preset, reset
  D_Flip_Flop d_ff_6 (.D(multiplexer_6_out), .clk(reg_clk), .Q(reg_int_out[2]));  // open: Qn, preset, reset
  assign reg_out[3] = reg_out_en ? reg_int_out[3] : 1'bz;  // Controlled_Buffer controlled_buffer_5
  Multiplexer multiplexer_7 (.in0(reg_int_out[1]), .in1(reg_in[1]), .out(multiplexer_7_out), .sel(reg_in_en));
  D_Flip_Flop d_ff_7 (.D(multiplexer_7_out), .clk(reg_clk), .Q(reg_int_out[1]));  // open: Qn, preset, reset
  assign reg_out[2] = reg_out_en ? reg_int_out[2] : 1'bz;  // Controlled_Buffer controlled_buffer_6
  Multiplexer multiplexer_8 (.in0(reg_int_out[0]), .in1(reg_in[0]), .out(multiplexer_8_out), .sel(reg_in_en));
  D_Flip_Flop d_ff_8 (.D(multiplexer_8_out), .clk(reg_clk), .Q(reg_int_out[0]));  // open: Qn, preset, reset
  assign reg_out[1] = reg_out_en ? reg_int_out[1] : 1'bz;  // Controlled_Buffer controlled_buffer_7
  assign reg_out[0] = reg_out_en ? reg_int_out[0] : 1'bz;  // Controlled_Buffer controlled_buffer_8
endmodule

module alucus_1908034 (
  input  [7:0] alu_in_1,
  input  alu_out_en,
  input  [7:0] alu_in_2,
  input  alu_sub,
  output [7:0] alu_out,
  output alu_cout
);

  wire adder_2_cout, adder_3_cout, adder_4_cout, adder_5_cout, adder_6_cout, adder_7_cout, adder_8_cout,
       xor_1_out, xor_2_out, xor_3_out, xor_4_out, xor_5_out, xor_6_out, xor_7_out, xor_8_out;
  wire [7:0] adder_8_out;

  xor xor_1 (xor_1_out, alu_in_2[7], alu_sub);
  Adder #(.width(1)) adder_1 (
    .a(alu_in_1[7]), .b(xor_1_out), .out(adder_8_out[7]), .cin(adder_2_cout), .cout(alu_cout));
  xor xor_2 (xor_2_out, alu_in_2[6], alu_sub);
  Adder #(.width(1)) adder_2 (
    .a(alu_in_1[6]), .b(xor_2_out), .out(adder_8_out[6]), .cin(adder_3_cout), .cout(adder_2_cout));
  xor xor_3 (xor_3_out, alu_in_2[5], alu_sub);
  Adder #(.width(1)) adder_3 (
    .a(alu_in_1[5]), .b(xor_3_out), .out(adder_8_out[5]), .cin(adder_4_cout), .cout(adder_3_cout));
  xor xor_4 (xor_4_out, alu_in_2[4], alu_sub);
  Adder #(.width(1)) adder_4 (
    .a(alu_in_1[4]), .b(xor_4_out), .out(adder_8_out[4]), .cin(adder_5_cout), .cout(adder_4_cout));
  xor xor_5 (xor_5_out, alu_in_2[3], alu_sub);
  Adder #(.width(1)) adder_5 (
    .a(alu_in_1[3]), .b(xor_5_out), .out(adder_8_out[3]), .cin(adder_6_cout), .cout(adder_5_cout));
  xor xor_6 (xor_6_out, alu_in_2[2], alu_sub);
  Adder #(.width(1)) adder_6 (
    .a(alu_in_1[2]), .b(xor_6_out), .out(adder_8_out[2]), .cin(adder_7_cout), .cout(adder_6_cout));
  xor xor_7 (xor_7_out, alu_in_2[1], alu_sub);
  Adder #(.width(1)) adder_7 (
    .a(alu_in_1[1]), .b(xor_7_out), .out(adder_8_out[1]), .cin(adder_8_cout), .cout(adder_7_cout));
  xor xor_8 (xor_8_out, alu_in_2[0], alu_sub);
  Adder #(.width(1)) adder_8 (.a(alu_in_1[0]), .b(xor_8_out), .out(adder_8_out[0]), .cin(alu_sub), .cout(adder_8_cout));
  assign alu_out = alu_out_en ? adder_8_out : 8'bz;  // Controlled_Buffer controlled_buffer_1
endmodule

module progcocus_1908034 (
  input  pc_en,
  input  pc_clk,
  input  pc_reset,
  input  pc_out_en,
  output [3:0] pc_out
);

  wire j_k_ff_2_qn, j_k_ff_3_qn, j_k_ff_4_qn;
  wire [3:0] j_k_ff_4_q;

  J_K_Flip_Flop j_k_ff_1 (
    .J(pc_en), .K(pc_en), .clk(j_k_ff_2_qn), .Q(j_k_ff_4_q[3]), .reset(pc_reset));  // open: Qn, preset
  J_K_Flip_Flop j_k_ff_2 (
    .J(pc_en), .K(pc_en), .clk(j_k_ff_3_qn), .Q(j_k_ff_4_q[2]), .Qn(j_k_ff_2_qn), .reset(pc_reset));  // open: preset
  J_K_Flip_Flop j_k_ff_3 (
    .J(pc_en), .K(pc_en), .clk(j_k_ff_4_qn), .Q(j_k_ff_4_q[1]), .Qn(j_k_ff_3_qn), .reset(pc_reset));  // open: preset
  J_K_Flip_Flop j_k_ff_4 (
    .J(pc_en), .K(pc_en), .clk(pc_clk), .Q(j_k_ff_4_q[0]), .Qn(j_k_ff_4_qn), .reset(pc_reset));  // open: preset
  assign pc_out = pc_out_en ? j_k_ff_4_q : 4'bz;  // Controlled_Buffer controlled_buffer_1
endmodule

module dec_4x16_1908034 (
  input  [3:0] dec_sec,
  output [15:0] dec_out
);

  wire not_1_out, not_2_out, not_3_out, not_4_out;

  not not_1 (not_1_out, dec_sec[3]);
  not not_2 (not_2_out, dec_sec[2]);
  not not_3 (not_3_out, dec_sec[1]);
  not not_4 (not_4_out, dec_sec[0]);
  and and_1 (dec_out[0], not_4_out, not_3_out, not_2_out, not_1_out);
  and and_2 (dec_out[1], dec_sec[0], not_3_out, not_2_out, not_1_out);
  and and_3 (dec_out[2], not_4_out, dec_sec[1], not_2_out, not_1_out);
  and and_4 (dec_out[3], dec_sec[0], dec_sec[1], not_2_out, not_1_out);
  and and_5 (dec_out[4], not_4_out, not_3_out, dec_sec[2], not_1_out);
  and and_6 (dec_out[5], dec_sec[0], not_3_out, dec_sec[2], not_1_out);
  and and_7 (dec_out[6], not_4_out, dec_sec[1], dec_sec[2], not_1_out);
  and and_8 (dec_out[7], dec_sec[0], dec_sec[1], dec_sec[2], not_1_out);
  and and_9 (dec_out[8], not_4_out, not_3_out, not_2_out, dec_sec[3]);
  and and_10 (dec_out[9], dec_sec[0], not_3_out, not_2_out, dec_sec[3]);
  and and_11 (dec_out[10], not_4_out, dec_sec[1], not_2_out, dec_sec[3]);
  and and_12 (dec_out[11], dec_sec[0], dec_sec[1], not_2_out, dec_sec[3]);
  and and_13 (dec_out[12], not_4_out, not_3_out, dec_sec[2], dec_sec[3]);
  and and_14 (dec_out[13], dec_sec[0], not_3_out, dec_sec[2], dec_sec[3]);
  and and_15 (dec_out[14], not_4_out, dec_sec[1], dec_sec[2], dec_sec[3]);
  and and_16 (dec_out[15], dec_sec[0], dec_sec[1], dec_sec[2], dec_sec[3]);
endmodule

module sram_celll_1908034 (
  input  [7:0] data_in,
  input  wr_en,
  input  clk,
  input  cs,
  input  rd_en,
  output [7:0] memory_content,
  output [7:0] data_out
);

  wire and_1_out, and_2_out;

  and and_1 (and_1_out, wr_en, cs);
  and and_2 (and_2_out, cs, rd_en);
  regcus_1908034 sramcell (
    .reg_in(data_in), .reg_in_en(and_1_out), .reg_clk(clk), .reg_out_en(and_2_out),
    .reg_int_out(memory_content), .reg_out(data_out));
endmodule

module sram_1908034 (
  input  sram_wr,
  input  sram_rd,
  input  [7:0] mar_d_in,
  input  [7:0] sram_d_in,
  input  mar_in_en,
  input  sram_clk,
  output [7:0] sram_d_out,
  output [7:0] out_8,
  output [7:0] out_9,
  output [7:0] out_10,
  output [7:0] out_11,
  output [7:0] out_12,
  output [7:0] out_13,
  output [7:0] out_14,
  output [7:0] out_15,
  output [7:0] out_16,
  output [7:0] out_17,
  output [7:0] out_18,
  output [7:0] out_19,
  output [7:0] out_20,
  output [7:0] out_21,
  output [7:0] out_22,
  output [7:0] out_23
);

  wire [7:0] controlled_buffer_1_out, regcus_1908034_1_reg_int_out;
  wire [15:0] dec_4x16_1908034_1_dec_out;

  regcus_1908034 regcus_1908034_1 (
    .reg_in(mar_d_in), .reg_in_en(mar_in_en), .reg_clk(sram_clk), .reg_int_out(regcus_1908034_1_reg_int_out));  // open: reg_out_en, reg_out
  dec_4x16_1908034 dec_4x16_1908034_1 (
    .dec_sec(regcus_1908034_1_reg_int_out[3:0]), .dec_out(dec_4x16_1908034_1_dec_out));
  assign controlled_buffer_1_out = sram_wr ? sram_d_in : 8'bz;  // Controlled_Buffer controlled_buffer_1
  sram_celll_1908034 sram_celll_1908034_1 (
    .data_in(controlled_buffer_1_out), .wr_en(sram_wr), .clk(sram_clk), .cs(dec_4x16_1908034_1_dec_out[0]),
    .rd_en(sram_rd), .memory_content(out_8), .data_out(controlled_buffer_1_out));
  sram_celll_1908034 sram_celll_1908034_2 (
    .data_in(controlled_buffer_1_out), .wr_en(sram_wr), .clk(sram_clk), .cs(dec_4x16_1908034_1_dec_out[1]),
    .rd_en(sram_rd), .memory_content(out_9), .data_out(controlled_buffer_1_out));
  sram_celll_1908034 sram_celll_1908034_3 (
    .data_in(controlled_buffer_1_out), .wr_en(sram_wr), .clk(sram_clk), .cs(dec_4x16_1908034_1_dec_out[2]),
    .rd_en(sram_rd), .memory_content(out_10), .data_out(controlled_buffer_1_out));
  sram_celll_1908034 sram_celll_1908034_4 (
    .data_in(controlled_buffer_1_out), .wr_en(sram_wr), .clk(sram_clk), .cs(dec_4x16_1908034_1_dec_out[3]),
    .rd_en(sram_rd), .memory_content(out_11), .data_out(controlled_buffer_1_out));
  sram_celll_1908034 sram_celll_1908034_5 (
    .data_in(controlled_buffer_1_out), .wr_en(sram_wr), .clk(sram_clk), .cs(dec_4x16_1908034_1_dec_out[4]),
    .rd_en(sram_rd), .memory_content(out_12), .data_out(controlled_buffer_1_out));
  sram_celll_1908034 sram_celll_1908034_6 (
    .data_in(controlled_buffer_1_out), .wr_en(sram_wr), .clk(sram_clk), .cs(dec_4x16_1908034_1_dec_out[5]),
    .rd_en(sram_rd), .memory_content(out_13), .data_out(controlled_buffer_1_out));
  sram_celll_1908034 sram_celll_1908034_7 (
    .data_in(controlled_buffer_1_out), .wr_en(sram_wr), .clk(sram_clk), .cs(dec_4x16_1908034_1_dec_out[6]),
    .rd_en(sram_rd), .memory_content(out_14), .data_out(controlled_buffer_1_out));
  sram_celll_1908034 sram_celll_1908034_8 (
    .data_in(controlled_buffer_1_out), .wr_en(sram_wr), .clk(sram_clk), .cs(dec_4x16_1908034_1_dec_out[7]),
    .rd_en(sram_rd), .memory_content(out_15), .data_out(controlled_buffer_1_out));
  sram_celll_1908034 sram_celll_1908034_9 (
    .data_in(controlled_buffer_1_out), .wr_en(sram_wr), .clk(sram_clk), .cs(dec_4x16_1908034_1_dec_out[8]),
    .rd_en(sram_rd), .memory_content(out_16), .data_out(controlled_buffer_1_out));
  sram_celll_1908034 sram_celll_1908034_10 (
    .data_in(controlled_buffer_1_out), .wr_en(sram_wr), .clk(sram_clk), .cs(dec_4x16_1908034_1_dec_out[9]),
    .rd_en(sram_rd), .memory_content(out_17), .data_out(controlled_buffer_1_out));
  sram_celll_1908034 sram_celll_1908034_11 (
    .data_in(controlled_buffer_1_out), .wr_en(sram_wr), .clk(sram_clk), .cs(dec_4x16_1908034_1_dec_out[10]),
    .rd_en(sram_rd), .memory_content(out_18), .data_out(controlled_buffer_1_out));
  sram_celll_1908034 sram_celll_1908034_12 (
    .data_in(controlled_buffer_1_out), .wr_en(sram_wr), .clk(sram_clk), .cs(dec_4x16_1908034_1_dec_out[11]),
    .rd_en(sram_rd), .memory_content(out_19), .data_out(controlled_buffer_1_out));
  sram_celll_1908034 sram_celll_1908034_13 (
    .data_in(controlled_buffer_1_out), .wr_en(sram_wr), .clk(sram_clk), .cs(dec_4x16_1908034_1_dec_out[12]),
    .rd_en(sram_rd), .memory_content(out_20), .data_out(controlled_buffer_1_out));
  sram_celll_1908034 sram_celll_1908034_14 (
    .data_in(controlled_buffer_1_out), .wr_en(sram_wr), .clk(sram_clk), .cs(dec_4x16_1908034_1_dec_out[13]),
    .rd_en(sram_rd), .memory_content(out_21), .data_out(controlled_buffer_1_out));
  sram_celll_1908034 sram_celll_1908034_15 (
    .data_in(controlled_buffer_1_out), .wr_en(sram_wr), .clk(sram_clk), .cs(dec_4x16_1908034_1_dec_out[14]),
    .rd_en(sram_rd), .memory_content(out_22), .data_out(controlled_buffer_1_out));
  sram_celll_1908034 sram_celll_1908034_16 (
    .data_in(controlled_buffer_1_out), .wr_en(sram_wr), .clk(sram_clk), .cs(dec_4x16_1908034_1_dec_out[15]),
    .rd_en(sram_rd), .memory_content(out_23), .data_out(controlled_buffer_1_out));
  assign sram_d_out = sram_rd ? controlled_buffer_1_out : 8'bz;  // Controlled_Buffer controlled_buffer_2
endmodule

module ins_reg_1908034 (
  input  [7:0] ins_reg_in,
  input  ins_reg_in_en,
  input  clk,
  input  ins_reg_out_en,
  output [3:0] add_outs,
  output [3:0] ins_out
);

  wire [3:0] regcus_1908034_1_reg_int_out;

  regcus_1908034 regcus_1908034_1 (
    .reg_in(ins_reg_in), .reg_in_en(ins_reg_in_en), .reg_clk(clk),
    .reg_int_out({ins_out, regcus_1908034_1_reg_int_out}));  // open: reg_out_en, reg_out
  assign add_outs = ins_reg_out_en ? regcus_1908034_1_reg_int_out : 4'bz;  // Controlled_Buffer controlled_buffer_1
endmodule

module ringcounter_1908034 (
  input  clk,
  input  clr,
  output t1,
  output t2,
  output t3,
  output t4,
  output t5,
  output t6
);

  wire not_1_out;

  not not_1 (not_1_out, clr);
  D_Flip_Flop d_ff_1 (.D(t6), .clk(clk), .Q(t1), .preset(not_1_out));  // open: Qn, reset
  D_Flip_Flop d_ff_2 (.D(t1), .clk(clk), .Q(t2), .reset(not_1_out));  // open: Qn, preset
  D_Flip_Flop d_ff_3 (.D(t2), .clk(clk), .Q(t3), .reset(not_1_out));  // open: Qn, preset
  D_Flip_Flop d_ff_4 (.D(t3), .clk(clk), .Q(t4), .reset(not_1_out));  // open: Qn, preset
  D_Flip_Flop d_ff_5 (.D(t4), .clk(clk), .Q(t5), .reset(not_1_out));  // open: Qn, preset
  D_Flip_Flop d_ff_6 (.D(t5), .clk(clk), .Q(t6), .reset(not_1_out));  // open: Qn, preset
endmodule

module DEC_1908034 (
  input  i7,
  input  i6,
  input  i5,
  input  i4,
  output out_5,
  output LDA,
  output ADD,
  output SUB,
  output AC_OUT,
  output STR,
  output LDB,
  output out_12,
  output out_13,
  output out_14,
  output out_15,
  output out_16,
  output out_17,
  output out_18,
  output out_19,
  output HLT
);

  wire and_1_out, and_2_out, and_3_out, and_4_out, and_5_out, and_6_out, and_7_out, and_16_out, not_1_out,
       not_2_out, not_3_out, not_4_out;

  not not_1 (not_1_out, i7);
  not not_2 (not_2_out, i6);
  not not_3 (not_3_out, i5);
  not not_4 (not_4_out, i4);
  and and_1 (and_1_out, not_4_out, not_3_out, not_2_out, not_1_out);
  buf buffer_1 (out_5, and_1_out);
  and and_2 (and_2_out, i4, not_3_out, not_2_out, not_1_out);
  buf buffer_2 (LDA, and_2_out);
  and and_3 (and_3_out, not_4_out, i5, not_2_out, not_1_out);
  buf buffer_3 (ADD, and_3_out);
  and and_4 (and_4_out, i4, i5, not_2_out, not_1_out);
  buf buffer_4 (SUB, and_4_out);
  and and_5 (and_5_out, not_4_out, not_3_out, i6, not_1_out);
  buf buffer_5 (AC_OUT, and_5_out);
  and and_6 (and_6_out, i4, not_3_out, i6, not_1_out);
  buf buffer_6 (STR, and_6_out);
  and and_7 (and_7_out, not_4_out, i5, i6, not_1_out);
  buf buffer_7 (LDB, and_7_out);
  and and_8 (out_12, i4, i5, i6, not_1_out);
  and and_9 (out_13, not_4_out, not_3_out, not_2_out, i7);
  and and_10 (out_14, i4, not_3_out, not_2_out, i7);
  and and_11 (out_15, not_4_out, i5, not_2_out, i7);
  and and_12 (out_16, i4, i5, not_2_out, i7);
  and and_13 (out_17, not_4_out, not_3_out, i6, i7);
  and and_14 (out_18, i4, not_3_out, i6, i7);
  and and_15 (out_19, not_4_out, i5, i6, i7);
  and and_16 (and_16_out, i4, i5, i6, i7);
  buf buffer_8 (HLT, and_16_out);
endmodule

module controlsequencer_1908034 (
  input  clk,
  input  clr,
  input  [3:0] in_3,
  input  BI_en,
  input  AI_en,
  input  SU_en,
  input  EO_en,
  input  RI_en,
  input  CO_en,
  input  CE_en,
  input  RO_en,
  input  MI_en,
  input  IO_en,
  input  II_en,
  input  OO_en,
  input  OI_en,
  input  AO_en,
  output t1,
  output t2,
  output t3,
  output t4,
  output t5,
  output t6,
  output out_24,
  output SU,
  output CO,
  output MI,
  output AI,
  output BI,
  output EO,
  output CE,
  output II,
  output RO,
  output OI,
  output RI,
  output OO,
  output I0,
  output AO
);

  wire and_1_out, and_2_out, and_3_out, and_4_out, and_5_out, and_6_out, and_7_out, and_8_out, and_9_out,
       and_10_out, and_11_out, and_12_out, and_13_out, and_14_out, and_15_out, and_16_out, and_17_out,
       and_18_out, and_19_out, and_20_out, and_21_out, and_22_out, and_23_out, and_24_out, and_25_out,
       and_26_out, and_27_out, and_28_out, and_29_out, dec_1908034_1_ac_out, dec_1908034_1_add,
       dec_1908034_1_lda, dec_1908034_1_ldb, dec_1908034_1_str, dec_1908034_1_sub, or_1_out, or_2_out,
       or_3_out, or_4_out, or_5_out, or_6_out, or_7_out;

  ringcounter_1908034 ringcounter_1908034_1 (
    .clk(clk), .clr(clr), .t1(t1), .t2(t2), .t3(t3), .t4(t4), .t5(t5), .t6(t6));
  DEC_1908034 dec_1908034_1 (
    .i7(in_3[3]), .i6(in_3[2]), .i5(in_3[1]), .i4(in_3[0]), .LDA(dec_1908034_1_lda), .ADD(dec_1908034_1_add),
    .SUB(dec_1908034_1_sub), .AC_OUT(dec_1908034_1_ac_out), .STR(dec_1908034_1_str), .LDB(dec_1908034_1_ldb),
    .HLT(out_24));  // open: out_5, out_12, out_13, out_14, out_15, out_16, out_17, out_18, out_19
  assign CO = CO_en ? t1 : 1'bz;  // Controlled_Buffer controlled_buffer_1
  and and_1 (and_1_out, dec_1908034_1_lda, t4);
  and and_2 (and_2_out, dec_1908034_1_add, t4);
  and and_3 (and_3_out, t4, dec_1908034_1_sub);
  and and_4 (and_4_out, t4, dec_1908034_1_str);
  and and_5 (and_5_out, t4, dec_1908034_1_ldb);
  or or_1 (or_1_out, t1, and_1_out, and_2_out, and_3_out, and_4_out, and_5_out);
  assign MI = MI_en ? or_1_out : 1'bz;  // Controlled_Buffer controlled_buffer_2
  assign CE = CE_en ? t3 : 1'bz;  // Controlled_Buffer controlled_buffer_3
  and and_6 (and_6_out, dec_1908034_1_lda, t5);
  assign II = II_en ? t2 : 1'bz;  // Controlled_Buffer controlled_buffer_4
  and and_7 (and_7_out, dec_1908034_1_add, t5);
  or or_2 (or_2_out, t2, and_6_out, and_7_out, and_8_out, and_9_out);
  assign RO = RO_en ? or_2_out : 1'bz;  // Controlled_Buffer controlled_buffer_5
  and and_8 (and_8_out, dec_1908034_1_sub, t5);
  and and_9 (and_9_out, dec_1908034_1_ldb, t5);
  and and_10 (and_10_out, dec_1908034_1_lda, t4);
  and and_11 (and_11_out, dec_1908034_1_add, t4);
  and and_12 (and_12_out, dec_1908034_1_sub, t4);
  or or_3 (or_3_out, and_10_out, and_11_out, and_12_out, and_13_out, and_14_out);
  assign I0 = IO_en ? or_3_out : 1'bz;  // Controlled_Buffer controlled_buffer_6
  and and_13 (and_13_out, dec_1908034_1_str, t4);
  and and_14 (and_14_out, dec_1908034_1_ldb, t4);
  and and_15 (and_15_out, t5, dec_1908034_1_lda);
  and and_16 (and_16_out, t6, dec_1908034_1_add);
  or or_4 (or_4_out, and_15_out, and_16_out, and_17_out);
  assign AI = AI_en ? or_4_out : 1'bz;  // Controlled_Buffer controlled_buffer_7
  and and_17 (and_17_out, t6, dec_1908034_1_sub);
  and and_18 (and_18_out, t5, dec_1908034_1_ldb);
  or or_5 (or_5_out, and_18_out, and_19_out, and_20_out);
  assign BI = BI_en ? or_5_out : 1'bz;  // Controlled_Buffer controlled_buffer_8
  and and_19 (and_19_out, t5, dec_1908034_1_add);
  and and_20 (and_20_out, t5, dec_1908034_1_sub);
  and and_21 (and_21_out, t6, dec_1908034_1_add);
  or or_6 (or_6_out, and_21_out, and_22_out, and_23_out, and_25_out);
  assign EO = EO_en ? or_6_out : 1'bz;  // Controlled_Buffer controlled_buffer_9
  and and_22 (and_22_out, t6, dec_1908034_1_sub);
  and and_23 (and_23_out, t6, dec_1908034_1_ldb);
  and and_24 (and_24_out, t6, dec_1908034_1_sub);
  and and_25 (and_25_out, t5, dec_1908034_1_str);
  assign SU = SU_en ? and_24_out : 1'bz;  // Controlled_Buffer controlled_buffer_10
  and and_26 (and_26_out, t4, dec_1908034_1_ac_out);
  and and_27 (and_27_out, t4, dec_1908034_1_ac_out);
  and and_28 (and_28_out, t5, dec_1908034_1_str);
  or or_7 (or_7_out, and_27_out, and_28_out);
  assign AO = AO_en ? and_26_out : 1'bz;  // Controlled_Buffer controlled_buffer_11
  and and_29 (and_29_out, t6, dec_1908034_1_str);
  assign RI = RI_en ? and_29_out : 1'bz;  // Controlled_Buffer controlled_buffer_12
  assign OI = OI_en ? or_7_out : 1'bz;  // Controlled_Buffer controlled_buffer_13
  assign OO = OO_en ? and_29_out : 1'bz;  // Controlled_Buffer controlled_buffer_14
endmodule
